// Logisim project NC16.circ as structural Verilog: 1 circuit, main circuit main
module main (
);

  wire adder_1_cout, and_1_out, and_2_out, and_3_out, and_4_out, clock_1_out, d_ff_1_q, d_ff_2_q,
       decoder_1_out0, decoder_1_out1, decoder_1_out2, decoder_1_out3, decoder_1_out4, decoder_1_out5,
       decoder_1_out6, decoder_1_out7, decoder_1_out8, multiplexer_8_out, not_1_out, not_2_out, not_3_out,
       not_4_out, not_6_out, not_7_out, not_8_out, not_10_out, not_11_out, not_12_out, not_13_out,
       not_14_out, not_15_out, not_16_out, not_17_out, not_18_out, not_19_out, not_20_out, not_21_out,
       not_22_out, not_23_out, not_24_out, not_25_out, RESET_out;
  wire [0:0] not_5_out;
  wire [1:0] counter_1_q, subtractor_1_bout;
  wire [2:0] shift_register_1_p6;
  wire [3:0] Instruction_Decorder_out_2;
  wire [15:0] A_q, adder_1_out, and_6_out, B_q, BP_q, C_q, D_q, demultiplexer_1_out0, demultiplexer_1_out1,
       demultiplexer_2_out0, demultiplexer_2_out1, demultiplexer_2_out2, demultiplexer_2_out3,
       demultiplexer_2_out4, demultiplexer_2_out5, demultiplexer_2_out6, demultiplexer_2_out7,
       demultiplexer_3_out0, demultiplexer_3_out1, demultiplexer_3_out2, demultiplexer_3_out3,
       demultiplexer_3_out4, demultiplexer_3_out6, demultiplexer_3_out7, divider_1_out, E_q, Input_data_sw16,
       multiplexer_1_out, multiplexer_2_out, multiplexer_3_out, multiplexer_4_out, multiplexer_5_out,
       multiplexer_6_out, multiplexer_7_out, multiplexer_9_out, multiplexer_10_out, multiplexer_11_out,
       multiplexer_12_out, multiplexer_13_out, multiplexer_15_out, multiplexer_16_out, multiplexer_17_out,
       multiplier_1_out, not_9_out, or_1_out, Output_port_q, PC_q, ram_1_dout, register_1_q,
       shift_register_1_p3, shift_register_1_p4, shift_register_1_p5, SP_q, subtractor_1_out, xor_1_out;
  wire [15:2] FLAGS_q;
  wire [18:0] Instruction_Decorder_out;
  wire [18:16] and_5_out;

  DipSwitch #(.number(16)) Input_data (
    .sw1(Input_data_sw16[15]), .sw2(Input_data_sw16[14]), .sw3(Input_data_sw16[13]),
    .sw4(Input_data_sw16[12]), .sw5(Input_data_sw16[11]), .sw6(Input_data_sw16[10]),
    .sw7(Input_data_sw16[9]), .sw8(Input_data_sw16[8]), .sw9(Input_data_sw16[7]), .sw10(Input_data_sw16[6]),
    .sw11(Input_data_sw16[5]), .sw12(Input_data_sw16[4]), .sw13(Input_data_sw16[3]),
    .sw14(Input_data_sw16[2]), .sw15(Input_data_sw16[1]), .sw16(Input_data_sw16[0]));
  Clock clock_1 (.out(clock_1_out));
  and and_1 (and_1_out, clock_1_out, not_8_out);
  Button RESET (.out(RESET_out));
  Decoder #(.select(4)) decoder_1 (
    .out0(decoder_1_out0), .out1(decoder_1_out1), .out2(decoder_1_out2), .out3(decoder_1_out3),
    .out4(decoder_1_out4), .out5(decoder_1_out5), .out6(decoder_1_out6), .out7(decoder_1_out7),
    .out8(decoder_1_out8), .sel(Instruction_Decorder_out[6:3]));  // open: out9, out10, out11, out12, out13, out14, out15, en
  LedBar #(.matrixcols(16)) ledbar_1 (
    .led0(multiplexer_15_out[15]), .led1(multiplexer_15_out[14]), .led2(multiplexer_15_out[13]),
    .led3(multiplexer_15_out[12]), .led4(multiplexer_15_out[11]), .led5(multiplexer_15_out[10]),
    .led6(multiplexer_15_out[9]), .led7(multiplexer_15_out[8]), .led8(multiplexer_15_out[7]),
    .led9(multiplexer_15_out[6]), .led10(multiplexer_15_out[5]), .led11(multiplexer_15_out[4]),
    .led12(multiplexer_15_out[3]), .led13(multiplexer_15_out[2]), .led14(multiplexer_15_out[1]),
    .led15(multiplexer_15_out[0]));
  Multiplexer #(.width(16)) multiplexer_1 (
    .in0(A_q), .in1(multiplexer_15_out), .out(multiplexer_1_out), .sel(decoder_1_out0));
  Multiplexer #(.width(16)) multiplexer_2 (
    .in0(B_q), .in1(multiplexer_15_out), .out(multiplexer_2_out), .sel(decoder_1_out1));
  Multiplexer #(.width(16)) multiplexer_3 (
    .in0(C_q), .in1(multiplexer_15_out), .out(multiplexer_3_out), .sel(decoder_1_out2));
  Multiplexer #(.width(16)) multiplexer_4 (
    .in0(D_q), .in1(multiplexer_15_out), .out(multiplexer_4_out), .sel(decoder_1_out3));
  Multiplexer #(.width(16)) multiplexer_5 (
    .in0(E_q), .in1(multiplexer_15_out), .out(multiplexer_5_out), .sel(decoder_1_out4));
  Multiplexer #(.width(16)) multiplexer_6 (
    .in0(BP_q), .in1(multiplexer_15_out), .out(multiplexer_6_out), .sel(decoder_1_out5));
  Multiplexer #(.width(16)) multiplexer_7 (
    .in0(SP_q), .in1(multiplexer_15_out), .out(multiplexer_7_out), .sel(decoder_1_out6));
  Multiplexer multiplexer_8 (.in0(decoder_1_out7), .in1(1'b1), .out(multiplexer_8_out), .sel(and_2_out));
  and and_2 (and_2_out, d_ff_1_q, not_1_out);
  not not_1 (not_1_out, not_2_out);
  Multiplexer #(.width(16)) multiplexer_9 (
    .in0(Output_port_q), .in1(multiplexer_15_out), .out(multiplexer_9_out), .sel(decoder_1_out8));
  Register #(.width(16)) A (.D(multiplexer_1_out), .en(decoder_1_out0), .clk(and_1_out), .Q(A_q), .clr(RESET_out));
  Register #(.width(16)) B (.D(multiplexer_2_out), .en(decoder_1_out1), .clk(and_1_out), .Q(B_q), .clr(RESET_out));
  Register #(.width(16)) C (.D(multiplexer_3_out), .en(decoder_1_out2), .clk(and_1_out), .Q(C_q), .clr(RESET_out));
  Register #(.width(16)) D (.D(multiplexer_4_out), .en(decoder_1_out3), .clk(and_1_out), .Q(D_q), .clr(RESET_out));
  Register #(.width(16)) E (.D(multiplexer_5_out), .en(decoder_1_out4), .clk(and_1_out), .Q(E_q), .clr(RESET_out));
  Register #(.width(16)) BP (.D(multiplexer_6_out), .en(decoder_1_out5), .clk(and_1_out), .Q(BP_q), .clr(RESET_out));
  Register #(.width(16)) SP (.D(multiplexer_7_out), .en(decoder_1_out6), .clk(and_1_out), .Q(SP_q), .clr(RESET_out));
  Counter #(.max('hffff), .width(16)) PC (
    .clr(RESET_out), .load(multiplexer_8_out), .clk(and_1_out), .D(multiplexer_11_out), .Q(PC_q));  // open: up, count, carry
  Multiplexer #(.width(16)) multiplexer_10 (
    .in0(PC_q), .in1(multiplexer_15_out), .out(multiplexer_10_out), .sel(multiplexer_8_out));
  Multiplexer #(.width(16)) multiplexer_11 (
    .in0(multiplexer_10_out), .in1(register_1_q), .out(multiplexer_11_out), .sel(and_2_out));
  Register #(.width(16)) Output_port (
    .D(multiplexer_9_out), .en(decoder_1_out8), .clk(and_1_out), .Q(Output_port_q), .clr(RESET_out));
  LedBar #(.matrixcols(16)) ledbar_2 (
    .led0(Output_port_q[15]), .led1(Output_port_q[14]), .led2(Output_port_q[13]), .led3(Output_port_q[12]),
    .led4(Output_port_q[11]), .led5(Output_port_q[10]), .led6(Output_port_q[9]), .led7(Output_port_q[8]),
    .led8(Output_port_q[7]), .led9(Output_port_q[6]), .led10(Output_port_q[5]), .led11(Output_port_q[4]),
    .led12(Output_port_q[3]), .led13(Output_port_q[2]), .led14(Output_port_q[1]), .led15(Output_port_q[0]));
  LedBar #(.matrixcols(16)) ledbar_3 (
    .led0(PC_q[15]), .led1(PC_q[14]), .led2(PC_q[13]), .led3(PC_q[12]), .led4(PC_q[11]), .led5(PC_q[10]),
    .led6(PC_q[9]), .led7(PC_q[8]), .led8(PC_q[7]), .led9(PC_q[6]), .led10(PC_q[5]), .led11(PC_q[4]),
    .led12(PC_q[3]), .led13(PC_q[2]), .led14(PC_q[1]), .led15(PC_q[0]));
  Register #(.width(16)) register_1 (.D(PC_q), .en(1'b1), .clk(and_1_out), .Q(register_1_q), .clr(RESET_out));
  not not_2 (not_2_out, and_3_out);
  and and_3 (and_3_out, not_3_out, not_4_out);
  D_Flip_Flop d_ff_1 (.D(not_2_out), .clk(and_1_out), .Q(d_ff_1_q), .reset(RESET_out));  // open: Qn, preset
  not not_3 (not_3_out, Instruction_Decorder_out[1]);
  not not_4 (not_4_out, Instruction_Decorder_out[2]);
  Multiplexer #(.select(2), .width(16)) multiplexer_12 (
    .in0(PC_q), .in1(A_q), .in2(shift_register_1_p4), .out(multiplexer_12_out),
    .sel(Instruction_Decorder_out[2:1]));  // open: in3
  RAM #(.addrWidth(16), .dataWidth(16), .enables("line")) ram_1 (
    .addr(multiplexer_12_out), .we(Instruction_Decorder_out[0]), .clk(and_1_out), .din(B_q), .dout(ram_1_dout));
  LedBar #(.matrixcols(16)) ledbar_4 (
    .led0(demultiplexer_1_out0[15]), .led1(demultiplexer_1_out0[14]), .led2(demultiplexer_1_out0[13]),
    .led3(demultiplexer_1_out0[12]), .led4(demultiplexer_1_out0[11]), .led5(demultiplexer_1_out0[10]),
    .led6(demultiplexer_1_out0[9]), .led7(demultiplexer_1_out0[8]), .led8(demultiplexer_1_out0[7]),
    .led9(demultiplexer_1_out0[6]), .led10(demultiplexer_1_out0[5]), .led11(demultiplexer_1_out0[4]),
    .led12(demultiplexer_1_out0[3]), .led13(demultiplexer_1_out0[2]), .led14(demultiplexer_1_out0[1]),
    .led15(demultiplexer_1_out0[0]));
  Multiplexer #(.select(4), .width(16)) multiplexer_13 (
    .in0(A_q), .in1(B_q), .in2(C_q), .in3(D_q), .in4(E_q), .in5(BP_q), .in6(SP_q), .in7(shift_register_1_p4),
    .in8(Input_data_sw16), .in9(ram_1_dout), .in10(PC_q), .out(multiplexer_13_out),
    .sel(Instruction_Decorder_out_2));  // open: in11, in12, in13, in14, in15
  // Shift_Register #(.length(2), .width(16)) shift_register_1: pin names not known; wires that end beside it: RESET_out, and_1_out, shift_register_1_p3, shift_register_1_p4, shift_register_1_p5, shift_register_1_p6, shift_register_1_p6
  Multiplexer #(.width(16)) multiplexer_14 (
    .in0(ram_1_dout), .in1({16{1'b1}}), .out(shift_register_1_p3), .sel(not_2_out));
  Counter #(.max('h3), .width(2)) counter_1 (
    .clr(RESET_out), .load(and_5_out[16]), .clk(and_1_out), .D({1'b0, not_5_out[0]}), .Q(counter_1_q));  // open: up, count, carry
  Multiplexer #(.width(16)) multiplexer_15 (
    .in0(demultiplexer_1_out0), .in1(multiplexer_17_out), .out(multiplexer_15_out),
    .sel(Instruction_Decorder_out[13]));
  Demultiplexer #(.width(16)) demultiplexer_1 (
    .out0(demultiplexer_1_out0), .out1(demultiplexer_1_out1), .in(multiplexer_13_out),
    .sel(Instruction_Decorder_out[13]));
  not not_5 (not_5_out[0], and_4_out);
  Demultiplexer #(.select(3), .width(16)) demultiplexer_2 (
    .out0(demultiplexer_2_out0), .out1(demultiplexer_2_out1), .out2(demultiplexer_2_out2),
    .out3(demultiplexer_2_out3), .out4(demultiplexer_2_out4), .out5(demultiplexer_2_out5),
    .out6(demultiplexer_2_out6), .out7(demultiplexer_2_out7), .in(demultiplexer_1_out1),
    .sel(Instruction_Decorder_out[9:7]));
  and and_4 (and_4_out, Instruction_Decorder_out[3], Instruction_Decorder_out[4], Instruction_Decorder_out[5], not_6_out);
  not not_6 (not_6_out, Instruction_Decorder_out[6]);
  Multiplexer #(.select(3), .width(16)) multiplexer_16 (
    .in0(A_q), .in1(B_q), .in2(C_q), .in3(D_q), .in4(E_q), .in5(BP_q), .in6(SP_q), .in7(shift_register_1_p4),
    .out(multiplexer_16_out), .sel(shift_register_1_p6));
  not not_7 (not_7_out, counter_1_q[0]);
  Demultiplexer #(.select(3), .width(16)) demultiplexer_3 (
    .out0(demultiplexer_3_out0), .out1(demultiplexer_3_out1), .out2(demultiplexer_3_out2),
    .out3(demultiplexer_3_out3), .out4(demultiplexer_3_out4), .out6(demultiplexer_3_out6),
    .out7(demultiplexer_3_out7), .in(multiplexer_16_out), .sel(Instruction_Decorder_out[9:7]));  // open: out5
  and and_5 (and_5_out[16], not_7_out, counter_1_q[1]);
  LED Instruction_Execute (.in(and_5_out[16]));
  PLA #(.in_width(19), .out_width(19), .\table ("xx0xxxxxxxxxxxxxxxx 0000000000001111000 # IE=0 (during fetch)\n0x10000110111111111 0011100000000111000 # jnz opd (Taken)\n1x10000110111111111 0000000000001111000 # jnz opd (Skip)\n1x10000111011111111 0011100000000111000 # jz opd (Taken)\n0x10000111011111111 0000000000001111000 # jz opd (Skip)\nx010000111111111111 0011100000000111000 # jns opd (Taken)\nx110000111111111111 0000000000001111000 # jns opd (Skip)\nx110001000011111111 0011100000000111000 # js opd (Taken)\nx010001000011111111 0000000000001111000 # js opd (Skip)\nxx10001000111111111 0011100000000111000 # jmp opd\n1x10001011011111111 0011100000000111000 # je opd (Taken)\n0x10001011011111111 0000000000001111000 # je opd (Skip)\n0x10001011111111111 0011100000000111000 # jne opd(Taken)\n1x10001011111111111 0000000000001111000 # jne opd(Skip)\n0010001100011111111 0011100000000111000 # ja opd (Taken)\nxx10001100011111111 0000000000001111000 # ja opd (Skip)\n0010001100111111111 0011100000000111000 # jae opd (Taken)\n1010001100111111111 0011100000000111000 # jae opd (Taken)\nxx10001100111111111 0000000000001111000 # jae opd (Skip)\n0110001101011111111 0011100000000111000 # jl opd (Taken)\nxx10001101011111111 0000000000001111000 # jl opd (Skip)\n0110001101111111111 0011100000000111000 # jle opd (Taken)\n1010001101111111111 0011100000000111000 # jle opd (Taken)\nxx10001101111111111 0000000000001111000 # jle opd (Skip)\nxx10000100001110001 0000100000001111011 # mov [a], b\nxx10000100001110001 0000100000001111101 # mov [opd], b\nxx10001001111111111 1000000000001111000 # hlt\nxx10001010011111111 0000000000001111000 # nop\nxxx1111111111111111 0000000000001111000 # invaild\nxx10001010111111111 0101000000000000000 # lpc\nxx10000000000000000 0000010000000000000 # add a, a\nxx10000000000000001 0000010010000000000 # add a, b\nxx10000000000000010 0000010100000000000 # add a, c\nxx10000000000000011 0000010110000000000 # add a, d\nxx10000000000000100 0000011000000000000 # add a, e\nxx10000000000000101 0000011010000000000 # add a, bp\nxx10000000000000110 0000011100000000000 # add a, sp\nxx10000000000010000 0000110000000001000 # add b, a\nxx10000000000010001 0000110010000001000 # add b, b\nxx10000000000010010 0000110100000001000 # add b, c\nxx10000000000010011 0000110110000001000 # add b, d\nxx10000000000010100 0000111000000001000 # add b, e\nxx10000000000010101 0000111010000001000 # add b, bp\nxx10000000000010110 0000111100000001000 # add b, sp\nxx10000000000100000 0001010000000010000 # add c, a\nxx10000000000100001 0001010010000010000 # add c, b\nxx10000000000100010 0001010100000010000 # add c, c\nxx10000000000100011 0001010110000010000 # add c, d\nxx10000000000100100 0001011000000010000 # add c, e\nxx10000000000100101 0001011010000010000 # add c, bp\nxx10000000000100110 0001011100000010000 # add c, sp\nxx10000000000110000 0001110000000011000 # add d, a\nxx10000000000110001 0001110010000011000 # add d, b\nxx10000000000110010 0001110100000011000 # add d, c\nxx10000000000110011 0001110110000011000 # add d, d\nxx10000000000110100 0001111000000011000 # add d, e\nxx10000000000110101 0001111010000011000 # add d, bp\nxx10000000000110110 0001111100000011000 # add d, sp\nxx10000000001000000 0010010000000100000 # add e, a\nxx10000000001000001 0010010010000100000 # add e, b\nxx10000000001000010 0010010100000100000 # add e, c\nxx10000000001000011 0010010110000100000 # add e, d\nxx10000000001000100 0010011000000100000 # add e, e\nxx10000000001000101 0010011010000100000 # add e, bp\nxx10000000001000110 0010011100000100000 # add e, sp\nxx10000000001010000 0010110000000101000 # add bp, a\nxx10000000001010001 0010110010000101000 # add bp, b\nxx10000000001010010 0010110100000101000 # add bp, c\nxx10000000001010011 0010110110000101000 # add bp, d\nxx10000000001010100 0010111000000101000 # add bp, e\nxx10000000001010101 0010111010000101000 # add bp, bp\nxx10000000001010110 0010111100000101000 # add bp, sp\nxx10000000001100000 0011010000000110000 # add sp, a\nxx10000000001100001 0011010010000110000 # add sp, b\nxx10000000001100010 0011010100000110000 # add sp, c\nxx10000000001100011 0011010110000110000 # add sp, d\nxx10000000001100100 0011011000000110000 # add sp, e\nxx10000000001100101 0011011010000110000 # add sp, bp\nxx10000000001100110 0011011100000110000 # add sp, sp\nxx10000000100000000 0000010000010000000 # sub a, a\nxx10000000100000001 0000010010010000000 # sub a, b\nxx10000000100000010 0000010100010000000 # sub a, c\nxx10000000100000011 0000010110010000000 # sub a, d\nxx10000000100000100 0000011000010000000 # sub a, e\nxx10000000100000101 0000011010010000000 # sub a, bp\nxx10000000100000110 0000011100010000000 # sub a, sp\nxx10000000100010000 0000110000010001000 # sub b, a\nxx10000000100010001 0000110010010001000 # sub b, b\nxx10000000100010010 0000110100010001000 # sub b, c\nxx10000000100010011 0000110110010001000 # sub b, d\nxx10000000100010100 0000111000010001000 # sub b, e\nxx10000000100010101 0000111010010001000 # sub b, bp\nxx10000000100010110 0000111100010001000 # sub b, sp\nxx10000000100100000 0001010000010010000 # sub c, a\nxx10000000100100001 0001010010010010000 # sub c, b\nxx10000000100100010 0001010100010010000 # sub c, c\nxx10000000100100011 0001010110010010000 # sub c, d\nxx10000000100100100 0001011000010010000 # sub c, e\nxx10000000100100101 0001011010010010000 # sub c, bp\nxx10000000100100110 0001011100010010000 # sub c, sp\nxx10000000100110000 0001110000010011000 # sub d, a\nxx10000000100110001 0001110010010011000 # sub d, b\nxx10000000100110010 0001110100010011000 # sub d, c\nxx10000000100110011 0001110110010011000 # sub d, d\nxx10000000100110100 0001111000010011000 # sub d, e\nxx10000000100110101 0001111010010011000 # sub d, bp\nxx10000000100110110 0001111100010011000 # sub d, sp\nxx10000000101000000 0010010000010100000 # sub e, a\nxx10000000101000001 0010010010010100000 # sub e, b\nxx10000000101000010 0010010100010100000 # sub e, c\nxx10000000101000011 0010010110010100000 # sub e, d\nxx10000000101000100 0010011000010100000 # sub e, e\nxx10000000101000101 0010011010010100000 # sub e, bp\nxx10000000101000110 0010011100010100000 # sub e, sp\nxx10000000101010000 0010110000010101000 # sub bp, a\nxx10000000101010001 0010110010010101000 # sub bp, b\nxx10000000101010010 0010110100010101000 # sub bp, c\nxx10000000101010011 0010110110010101000 # sub bp, d\nxx10000000101010100 0010111000010101000 # sub bp, e\nxx10000000101010101 0010111010010101000 # sub bp, bp\nxx10000000101010110 0010111100010101000 # sub bp, sp\nxx10000000101100000 0011010000010110000 # sub sp, a\nxx10000000101100001 0011010010010110000 # sub sp, b\nxx10000000101100010 0011010100010110000 # sub sp, c\nxx10000000101100011 0011010110010110000 # sub sp, d\nxx10000000101100100 0011011000010110000 # sub sp, e\nxx10000000101100101 0011011010010110000 # sub sp, bp\nxx10000000101100110 0011011100010110000 # sub sp, sp\nxx10000001000000000 0000010000100000000 # mul a, a\nxx10000001000000001 0000010010100000000 # mul a, b\nxx10000001000000010 0000010100100000000 # mul a, c\nxx10000001000000011 0000010110100000000 # mul a, d\nxx10000001000000100 0000011000100000000 # mul a, e\nxx10000001000000101 0000011010100000000 # mul a, bp\nxx10000001000000110 0000011100100000000 # mul a, sp\nxx10000001000010000 0000110000100001000 # mul b, a\nxx10000001000010001 0000110010100001000 # mul b, b\nxx10000001000010010 0000110100100001000 # mul b, c\nxx10000001000010011 0000110110100001000 # mul b, d\nxx10000001000010100 0000111000100001000 # mul b, e\nxx10000001000010101 0000111010100001000 # mul b, bp\nxx10000001000010110 0000111100100001000 # mul b, sp\nxx10000001000100000 0001010000100010000 # mul c, a\nxx10000001000100001 0001010010100010000 # mul c, b\nxx10000001000100010 0001010100100010000 # mul c, c\nxx10000001000100011 0001010110100010000 # mul c, d\nxx10000001000100100 0001011000100010000 # mul c, e\nxx10000001000100101 0001011010100010000 # mul c, bp\nxx10000001000100110 0001011100100010000 # mul c, sp\nxx10000001000110000 0001110000100011000 # mul d, a\nxx10000001000110001 0001110010100011000 # mul d, b\nxx10000001000110010 0001110100100011000 # mul d, c\nxx10000001000110011 0001110110100011000 # mul d, d\nxx10000001000110100 0001111000100011000 # mul d, e\nxx10000001000110101 0001111010100011000 # mul d, bp\nxx10000001000110110 0001111100100011000 # mul d, sp\nxx10000001001000000 0010010000100100000 # mul e, a\nxx10000001001000001 0010010010100100000 # mul e, b\nxx10000001001000010 0010010100100100000 # mul e, c\nxx10000001001000011 0010010110100100000 # mul e, d\nxx10000001001000100 0010011000100100000 # mul e, e\nxx10000001001000101 0010011010100100000 # mul e, bp\nxx10000001001000110 0010011100100100000 # mul e, sp\nxx10000001001010000 0010110000100101000 # mul bp, a\nxx10000001001010001 0010110010100101000 # mul bp, b\nxx10000001001010010 0010110100100101000 # mul bp, c\nxx10000001001010011 0010110110100101000 # mul bp, d\nxx10000001001010100 0010111000100101000 # mul bp, e\nxx10000001001010101 0010111010100101000 # mul bp, bp\nxx10000001001010110 0010111100100101000 # mul bp, sp\nxx10000001001100000 0011010000100110000 # mul sp, a\nxx10000001001100001 0011010010100110000 # mul sp, b\nxx10000001001100010 0011010100100110000 # mul sp, c\nxx10000001001100011 0011010110100110000 # mul sp, d\nxx10000001001100100 0011011000100110000 # mul sp, e\nxx10000001001100101 0011011010100110000 # mul sp, bp\nxx10000001001100110 0011011100100110000 # mul sp, sp\nxx10000001100000000 0000010000110000000 # and a, a\nxx10000001100000001 0000010010110000000 # and a, b\nxx10000001100000010 0000010100110000000 # and a, c\nxx10000001100000011 0000010110110000000 # and a, d\nxx10000001100000100 0000011000110000000 # and a, e\nxx10000001100000101 0000011010110000000 # and a, bp\nxx10000001100000110 0000011100110000000 # and a, sp\nxx10000001100010000 0000110000110001000 # and b, a\nxx10000001100010001 0000110010110001000 # and b, b\nxx10000001100010010 0000110100110001000 # and b, c\nxx10000001100010011 0000110110110001000 # and b, d\nxx10000001100010100 0000111000110001000 # and b, e\nxx10000001100010101 0000111010110001000 # and b, bp\nxx10000001100010110 0000111100110001000 # and b, sp\nxx10000001100100000 0001010000110010000 # and c, a\nxx10000001100100001 0001010010110010000 # and c, b\nxx10000001100100010 0001010100110010000 # and c, c\nxx10000001100100011 0001010110110010000 # and c, d\nxx10000001100100100 0001011000110010000 # and c, e\nxx10000001100100101 0001011010110010000 # and c, bp\nxx10000001100100110 0001011100110010000 # and c, sp\nxx10000001100110000 0001110000110011000 # and d, a\nxx10000001100110001 0001110010110011000 # and d, b\nxx10000001100110010 0001110100110011000 # and d, c\nxx10000001100110011 0001110110110011000 # and d, d\nxx10000001100110100 0001111000110011000 # and d, e\nxx10000001100110101 0001111010110011000 # and d, bp\nxx10000001100110110 0001111100110011000 # and d, sp\nxx10000001101000000 0010010000110100000 # and e, a\nxx10000001101000001 0010010010110100000 # and e, b\nxx10000001101000010 0010010100110100000 # and e, c\nxx10000001101000011 0010010110110100000 # and e, d\nxx10000001101000100 0010011000110100000 # and e, e\nxx10000001101000101 0010011010110100000 # and e, bp\nxx10000001101000110 0010011100110100000 # and e, sp\nxx10000001101010000 0010110000110101000 # and bp, a\nxx10000001101010001 0010110010110101000 # and bp, b\nxx10000001101010010 0010110100110101000 # and bp, c\nxx10000001101010011 0010110110110101000 # and bp, d\nxx10000001101010100 0010111000110101000 # and bp, e\nxx10000001101010101 0010111010110101000 # and bp, bp\nxx10000001101010110 0010111100110101000 # and bp, sp\nxx10000001101100000 0011010000110110000 # and sp, a\nxx10000001101100001 0011010010110110000 # and sp, b\nxx10000001101100010 0011010100110110000 # and sp, c\nxx10000001101100011 0011010110110110000 # and sp, d\nxx10000001101100100 0011011000110110000 # and sp, e\nxx10000001101100101 0011011010110110000 # and sp, bp\nxx10000001101100110 0011011100110110000 # and sp, sp\nxx10000010000000000 0000010001000000000 # or a, a\nxx10000010000000001 0000010011000000000 # or a, b\nxx10000010000000010 0000010101000000000 # or a, c\nxx10000010000000011 0000010111000000000 # or a, d\nxx10000010000000100 0000011001000000000 # or a, e\nxx10000010000000101 0000011011000000000 # or a, bp\nxx10000010000000110 0000011101000000000 # or a, sp\nxx10000010000010000 0000110001000001000 # or b, a\nxx10000010000010001 0000110011000001000 # or b, b\nxx10000010000010010 0000110101000001000 # or b, c\nxx10000010000010011 0000110111000001000 # or b, d\nxx10000010000010100 0000111001000001000 # or b, e\nxx10000010000010101 0000111011000001000 # or b, bp\nxx10000010000010110 0000111101000001000 # or b, sp\nxx10000010000100000 0001010001000010000 # or c, a\nxx10000010000100001 0001010011000010000 # or c, b\nxx10000010000100010 0001010101000010000 # or c, c\nxx10000010000100011 0001010111000010000 # or c, d\nxx10000010000100100 0001011001000010000 # or c, e\nxx10000010000100101 0001011011000010000 # or c, bp\nxx10000010000100110 0001011101000010000 # or c, sp\nxx10000010000110000 0001110001000011000 # or d, a\nxx10000010000110001 0001110011000011000 # or d, b\nxx10000010000110010 0001110101000011000 # or d, c\nxx10000010000110011 0001110111000011000 # or d, d\nxx10000010000110100 0001111001000011000 # or d, e\nxx10000010000110101 0001111011000011000 # or d, bp\nxx10000010000110110 0001111101000011000 # or d, sp\nxx10000010001000000 0010010001000100000 # or e, a\nxx10000010001000001 0010010011000100000 # or e, b\nxx10000010001000010 0010010101000100000 # or e, c\nxx10000010001000011 0010010111000100000 # or e, d\nxx10000010001000100 0010011001000100000 # or e, e\nxx10000010001000101 0010011011000100000 # or e, bp\nxx10000010001000110 0010011101000100000 # or e, sp\nxx10000010001010000 0010110001000101000 # or bp, a\nxx10000010001010001 0010110011000101000 # or bp, b\nxx10000010001010010 0010110101000101000 # or bp, c\nxx10000010001010011 0010110111000101000 # or bp, d\nxx10000010001010100 0010111001000101000 # or bp, e\nxx10000010001010101 0010111011000101000 # or bp, bp\nxx10000010001010110 0010111101000101000 # or bp, sp\nxx10000010001100000 0011010001000110000 # or sp, a\nxx10000010001100001 0011010011000110000 # or sp, b\nxx10000010001100010 0011010101000110000 # or sp, c\nxx10000010001100011 0011010111000110000 # or sp, d\nxx10000010001100100 0011011001000110000 # or sp, e\nxx10000010001100101 0011011011000110000 # or sp, bp\nxx10000010001100110 0011011101000110000 # or sp, sp\nxx10000011000000000 0000010001100000000 # xor a, a\nxx10000011000000001 0000010011100000000 # xor a, b\nxx10000011000000010 0000010101100000000 # xor a, c\nxx10000011000000011 0000010111100000000 # xor a, d\nxx10000011000000100 0000011001100000000 # xor a, e\nxx10000011000000101 0000011011100000000 # xor a, bp\nxx10000011000000110 0000011101100000000 # xor a, sp\nxx10000011000010000 0000110001100001000 # xor b, a\nxx10000011000010001 0000110011100001000 # xor b, b\nxx10000011000010010 0000110101100001000 # xor b, c\nxx10000011000010011 0000110111100001000 # xor b, d\nxx10000011000010100 0000111001100001000 # xor b, e\nxx10000011000010101 0000111011100001000 # xor b, bp\nxx10000011000010110 0000111101100001000 # xor b, sp\nxx10000011000100000 0001010001100010000 # xor c, a\nxx10000011000100001 0001010011100010000 # xor c, b\nxx10000011000100010 0001010101100010000 # xor c, c\nxx10000011000100011 0001010111100010000 # xor c, d\nxx10000011000100100 0001011001100010000 # xor c, e\nxx10000011000100101 0001011011100010000 # xor c, bp\nxx10000011000100110 0001011101100010000 # xor c, sp\nxx10000011000110000 0001110001100011000 # xor d, a\nxx10000011000110001 0001110011100011000 # xor d, b\nxx10000011000110010 0001110101100011000 # xor d, c\nxx10000011000110011 0001110111100011000 # xor d, d\nxx10000011000110100 0001111001100011000 # xor d, e\nxx10000011000110101 0001111011100011000 # xor d, bp\nxx10000011000110110 0001111101100011000 # xor d, sp\nxx10000011001000000 0010010001100100000 # xor e, a\nxx10000011001000001 0010010011100100000 # xor e, b\nxx10000011001000010 0010010101100100000 # xor e, c\nxx10000011001000011 0010010111100100000 # xor e, d\nxx10000011001000100 0010011001100100000 # xor e, e\nxx10000011001000101 0010011011100100000 # xor e, bp\nxx10000011001000110 0010011101100100000 # xor e, sp\nxx10000011001010000 0010110001100101000 # xor bp, a\nxx10000011001010001 0010110011100101000 # xor bp, b\nxx10000011001010010 0010110101100101000 # xor bp, c\nxx10000011001010011 0010110111100101000 # xor bp, d\nxx10000011001010100 0010111001100101000 # xor bp, e\nxx10000011001010101 0010111011100101000 # xor bp, bp\nxx10000011001010110 0010111101100101000 # xor bp, sp\nxx10000011001100000 0011010001100110000 # xor sp, a\nxx10000011001100001 0011010011100110000 # xor sp, b\nxx10000011001100010 0011010101100110000 # xor sp, c\nxx10000011001100011 0011010111100110000 # xor sp, d\nxx10000011001100100 0011011001100110000 # xor sp, e\nxx10000011001100101 0011011011100110000 # xor sp, bp\nxx10000011001100110 0011011101100110000 # xor sp, sp\nxx10000011100000000 0000010001110000000 # div a, a\nxx10000011100000001 0000010011110000000 # div a, b\nxx10000011100000010 0000010101110000000 # div a, c\nxx10000011100000011 0000010111110000000 # div a, d\nxx10000011100000100 0000011001110000000 # div a, e\nxx10000011100000101 0000011011110000000 # div a, bp\nxx10000011100000110 0000011101110000000 # div a, sp\nxx10000011100010000 0000110001110001000 # div b, a\nxx10000011100010001 0000110011110001000 # div b, b\nxx10000011100010010 0000110101110001000 # div b, c\nxx10000011100010011 0000110111110001000 # div b, d\nxx10000011100010100 0000111001110001000 # div b, e\nxx10000011100010101 0000111011110001000 # div b, bp\nxx10000011100010110 0000111101110001000 # div b, sp\nxx10000011100100000 0001010001110010000 # div c, a\nxx10000011100100001 0001010011110010000 # div c, b\nxx10000011100100010 0001010101110010000 # div c, c\nxx10000011100100011 0001010111110010000 # div c, d\nxx10000011100100100 0001011001110010000 # div c, e\nxx10000011100100101 0001011011110010000 # div c, bp\nxx10000011100100110 0001011101110010000 # div c, sp\nxx10000011100110000 0001110001110011000 # div d, a\nxx10000011100110001 0001110011110011000 # div d, b\nxx10000011100110010 0001110101110011000 # div d, c\nxx10000011100110011 0001110111110011000 # div d, d\nxx10000011100110100 0001111001110011000 # div d, e\nxx10000011100110101 0001111011110011000 # div d, bp\nxx10000011100110110 0001111101110011000 # div d, sp\nxx10000011101000000 0010010001110100000 # div e, a\nxx10000011101000001 0010010011110100000 # div e, b\nxx10000011101000010 0010010101110100000 # div e, c\nxx10000011101000011 0010010111110100000 # div e, d\nxx10000011101000100 0010011001110100000 # div e, e\nxx10000011101000101 0010011011110100000 # div e, bp\nxx10000011101000110 0010011101110100000 # div e, sp\nxx10000011101010000 0010110001110101000 # div bp, a\nxx10000011101010001 0010110011110101000 # div bp, b\nxx10000011101010010 0010110101110101000 # div bp, c\nxx10000011101010011 0010110111110101000 # div bp, d\nxx10000011101010100 0010111001110101000 # div bp, e\nxx10000011101010101 0010111011110101000 # div bp, bp\nxx10000011101010110 0010111101110101000 # div bp, sp\nxx10000011101100000 0011010001110110000 # div sp, a\nxx10000011101100001 0011010011110110000 # div sp, b\nxx10000011101100010 0011010101110110000 # div sp, c\nxx10000011101100011 0011010111110110000 # div sp, d\nxx10000011101100100 0011011001110110000 # div sp, e\nxx10000011101100101 0011011011110110000 # div sp, bp\nxx10000011101100110 0011011101110110000 # div sp, sp\nxx10000000000001111 0000011110000000000 # add a, opd\nxx10000000000011111 0000111110000001000 # add b, opd\nxx10000000000101111 0001011110000010000 # add c, opd\nxx10000000000111111 0001111110000011000 # add d, opd\nxx10000000001001111 0010011110000100000 # add e, opd\nxx10000000001011111 0010111110000101000 # add bp, opd\nxx10000000001101111 0011011110000110000 # add sp, opd\nxx10000000100001111 0000011110010000000 # sub a, opd\nxx10000000100011111 0000111110010001000 # sub b, opd\nxx10000000100101111 0001011110010010000 # sub c, opd\nxx10000000100111111 0001111110010011000 # sub d, opd\nxx10000000101001111 0010011110010100000 # sub e, opd\nxx10000000101011111 0010111110010101000 # sub bp, opd\nxx10000000101101111 0011011110010110000 # sub sp, opd\nxx10000001000001111 0000011110100000000 # mul a, opd\nxx10000001000011111 0000111110100001000 # mul b, opd\nxx10000001000101111 0001011110100010000 # mul c, opd\nxx10000001000111111 0001111110100011000 # mul d, opd\nxx10000001001001111 0010011110100100000 # mul e, opd\nxx10000001001011111 0010111110100101000 # mul bp, opd\nxx10000001001101111 0011011110100110000 # mul sp, opd\nxx10000001100001111 0000011110110000000 # and a, opd\nxx10000001100011111 0000111110110001000 # and b, opd\nxx10000001100101111 0001011110110010000 # and c, opd\nxx10000001100111111 0001111110110011000 # and d, opd\nxx10000001101001111 0010011110110100000 # and e, opd\nxx10000001101011111 0010111110110101000 # and bp, opd\nxx10000001101101111 0011011110110110000 # and sp, opd\nxx10000010000001111 0000011111000000000 # or a, opd\nxx10000010000011111 0000111111000001000 # or b, opd\nxx10000010000101111 0001011111000010000 # or c, opd\nxx10000010000111111 0001111111000011000 # or d, opd\nxx10000010001001111 0010011111000100000 # or e, opd\nxx10000010001011111 0010111111000101000 # or bp, opd\nxx10000010001101111 0011011111000110000 # or sp, opd\nxx10000011000001111 0000011111100000000 # xor a, opd\nxx10000011000011111 0000111111100001000 # xor b, opd\nxx10000011000101111 0001011111100010000 # xor c, opd\nxx10000011000111111 0001111111100011000 # xor d, opd\nxx10000011001001111 0010011111100100000 # xor e, opd\nxx10000011001011111 0010111111100101000 # xor bp, opd\nxx10000011001101111 0011011111100110000 # xor sp, opd\nxx10000011100001111 0000011111110000000 # div a, opd\nxx10000011100011111 0000111111110001000 # div b, opd\nxx10000011100101111 0001011111110010000 # div c, opd\nxx10000011100111111 0001111111110011000 # div d, opd\nxx10000011101001111 0010011111110100000 # div e, opd\nxx10000011101011111 0010111111110101000 # div bp, opd\nxx10000011101101111 0011011111110110000 # div sp, opd\nxx10000000000000111 0100010000000000010 # add a, [a]\nxx10000000000010111 0100010010000001010 # add b, [a]\nxx10000000000100111 0100010100000010010 # add c, [a]\nxx10000000000110111 0100010110000011010 # add d, [a]\nxx10000000001000111 0100011000000100010 # add e, [a]\nxx10000000001010111 0100011010000101010 # add bp, [a]\nxx10000000001100111 0100011100000110010 # add sp, [a]\nxx10000000100000111 0100010000010000010 # sub a, [a]\nxx10000000100010111 0100010010010001010 # sub b, [a]\nxx10000000100100111 0100010100010010010 # sub c, [a]\nxx10000000100110111 0100010110010011010 # sub d, [a]\nxx10000000101000111 0100011000010100010 # sub e, [a]\nxx10000000101010111 0100011010010101010 # sub bp, [a]\nxx10000000101100111 0100011100010110010 # sub sp, [a]\nxx10000001000000111 0100010000100000010 # mul a, [a]\nxx10000001000010111 0100010010100001010 # mul b, [a]\nxx10000001000100111 0100010100100010010 # mul c, [a]\nxx10000001000110111 0100010110100011010 # mul d, [a]\nxx10000001001000111 0100011000100100010 # mul e, [a]\nxx10000001001010111 0100011010100101010 # mul bp, [a]\nxx10000001001100111 0100011100100110010 # mul sp, [a]\nxx10000001100000111 0100010000110000010 # and a, [a]\nxx10000001100010111 0100010010110001010 # and b, [a]\nxx10000001100100111 0100010100110010010 # and c, [a]\nxx10000001100110111 0100010110110011010 # and d, [a]\nxx10000001101000111 0100011000110100010 # and e, [a]\nxx10000001101010111 0100011010110101010 # and bp, [a]\nxx10000001101100111 0100011100110110010 # and sp, [a]\nxx10000010000000111 0100010001000000010 # or a, [a]\nxx10000010000010111 0100010011000001010 # or b, [a]\nxx10000010000100111 0100010101000010010 # or c, [a]\nxx10000010000110111 0100010111000011010 # or d, [a]\nxx10000010001000111 0100011001000100010 # or e, [a]\nxx10000010001010111 0100011011000101010 # or bp, [a]\nxx10000010001100111 0100011101000110010 # or sp, [a]\nxx10000011000000111 0100010001100000010 # sub a, [a]\nxx10000011000010111 0100010011100001010 # sub b, [a]\nxx10000011000100111 0100010101100010010 # sub c, [a]\nxx10000011000110111 0100010111100011010 # sub d, [a]\nxx10000011001000111 0100011001100100010 # sub e, [a]\nxx10000011001010111 0100011011100101010 # sub bp, [a]\nxx10000011001100111 0100011101100110010 # sub sp, [a]\nxx10000011100000111 0100010001110000010 # div a, [a]\nxx10000011100010111 0100010011110001010 # div b, [a]\nxx10000011100100111 0100010101110010010 # div c, [a]\nxx10000011100110111 0100010111110011010 # div d, [a]\nxx10000011101000111 0100011001110100010 # div e, [a]\nxx10000011101010111 0100011011110101010 # div bp, [a]\nxx10000011101100111 0100011101110110010 # div sp, [a]\nxx10000010100001111 0000010001010000000 # not a\nxx10000010100011111 0000110001010001000 # not b\nxx10000010100101111 0001010001010010000 # not c\nxx10000010100111111 0001110001010011000 # not d\nxx10000010101001111 0010010001010100000 # not e\nxx10000010101011111 0010110001010101000 # not bp\nxx10000010101101111 0011010001010110000 # not sp\nxx10000100000000000 0000000000000000000 # mov a, a\nxx10000100000000001 0000100000000000000 # mov a, b\nxx10000100000000010 0001000000000000000 # mov a, c\nxx10000100000000011 0001100000000000000 # mov a, d\nxx10000100000000100 0010000000000000000 # mov a, e\nxx10000100000000101 0010100000000000000 # mov a, bp\nxx10000100000000110 0011000000000000000 # mov a, sp\nxx10000100000010000 0000000000000001000 # mov b, a\nxx10000100000010001 0000100000000001000 # mov b, b\nxx10000100000010010 0001000000000001000 # mov b, c\nxx10000100000010011 0001100000000001000 # mov b, d\nxx10000100000010100 0010000000000001000 # mov b, e\nxx10000100000010101 0010100000000001000 # mov b, bp\nxx10000100000010110 0011000000000001000 # mov b, sp\nxx10000100000100000 0000000000000010000 # mov c, a\nxx10000100000100001 0000100000000010000 # mov c, b\nxx10000100000100010 0001000000000010000 # mov c, c\nxx10000100000100011 0001100000000010000 # mov c, d\nxx10000100000100100 0010000000000010000 # mov c, e\nxx10000100000100101 0010100000000010000 # mov c, bp\nxx10000100000100110 0011000000000010000 # mov c, sp\nxx10000100000110000 0000000000000011000 # mov d, a\nxx10000100000110001 0000100000000011000 # mov d, b\nxx10000100000110010 0001000000000011000 # mov d, c\nxx10000100000110011 0001100000000011000 # mov d, d\nxx10000100000110100 0010000000000011000 # mov d, e\nxx10000100000110101 0010100000000011000 # mov d, bp\nxx10000100000110110 0011000000000011000 # mov d, sp\nxx10000100001000000 0000000000000100000 # mov e, a\nxx10000100001000001 0000100000000100000 # mov e, b\nxx10000100001000010 0001000000000100000 # mov e, c\nxx10000100001000011 0001100000000100000 # mov e, d\nxx10000100001000100 0010000000000100000 # mov e, e\nxx10000100001000101 0010100000000100000 # mov e, bp\nxx10000100001000110 0011000000000100000 # mov e, sp\nxx10000100001010000 0000000000000101000 # mov bp, a\nxx10000100001010001 0000100000000101000 # mov bp, b\nxx10000100001010010 0001000000000101000 # mov bp, c\nxx10000100001010011 0001100000000101000 # mov bp, d\nxx10000100001010100 0010000000000101000 # mov bp, e\nxx10000100001010101 0010100000000101000 # mov bp, bp\nxx10000100001010110 0011000000000101000 # mov bp, sp\nxx10000100001100000 0000000000000110000 # mov sp, a\nxx10000100001100001 0000100000000110000 # mov sp, b\nxx10000100001100010 0001000000000110000 # mov sp, c\nxx10000100001100011 0001100000000110000 # mov sp, d\nxx10000100001100100 0010000000000110000 # mov sp, e\nxx10000100001100101 0010100000000110000 # mov sp, bp\nxx10000100001100110 0011000000000110000 # mov sp, sp\nxx10000100000000111 0100100000000000010 # mov a, [a]\nxx10000100000010111 0100100000000001010 # mov b, [a]\nxx10000100000100111 0100100000000010010 # mov c, [a]\nxx10000100000110111 0100100000000011010 # mov d, [a]\nxx10000100001000111 0100100000000100010 # mov e, [a]\nxx10000100001010111 0100100000000101010 # mov bp, [a]\nxx10000100001100111 0100100000000110010 # mov sp, [a]\nxx10000100000001111 0011100000000000000 # mov a, opd\nxx10000100000011111 0011100000000001000 # mov b, opd\nxx10000100000101111 0011100000000010000 # mov c, opd\nxx10000100000111111 0011100000000011000 # mov d, opd\nxx10000100001001111 0011100000000100000 # mov e, opd\nxx10000100001011111 0011100000000101000 # mov bp, opd\nxx10000100001101111 0011100000000110000 # mov sp, opd\nxx10000100000000111 0100100000000000100 # mov a, [opd]\nxx10000100000010111 0100100000000001100 # mov b, [opd]\nxx10000100000100111 0100100000000010100 # mov c, [opd]\nxx10000100000110111 0100100000000011100 # mov d, [opd]\nxx10000100001000111 0100100000000100100 # mov e, [opd]\nxx10000100001010111 0100100000000101100 # mov bp, [opd]\nxx10000100001100111 0100100000000110100 # mov sp, [opd]\nxx10000100100001111 0100000000000000000 # in a\nxx10000100100011111 0100000000000001000 # in b\nxx10000100100101111 0100000000000010000 # in c\nxx10000100100111111 0100000000000011000 # in d\nxx10000100101001111 0100000000000100000 # in e\nxx10000100101011111 0100000000000101000 # in bp\nxx10000100101101111 0100000000000110000 # in sp\nxx10000101000001111 0000000000001000000 # out a\nxx10000101000011111 0000100000001000000 # out b\nxx10000101000101111 0001000000001000000 # out c\nxx10000101000111111 0001100000001000000 # out d\nxx10000101001001111 0010000000001000000 # out e\nxx10000101001011111 0010100000001000000 # out bp\nxx10000101001101111 0011000000001000000 # out sp\nxx10001001000000000 0000010000011111000 # cmp a, a\nxx10001001000000001 0000010010011111000 # cmp a, b\nxx10001001000000010 0000010100011111000 # cmp a, c\nxx10001001000000011 0000010110011111000 # cmp a, d\nxx10001001000000100 0000011000011111000 # cmp a, e\nxx10001001000000101 0000011010011111000 # cmp a, bp\nxx10001001000000110 0000011100011111000 # cmp a, sp\nxx10001001000010000 0000110000011111000 # cmp b, a\nxx10001001000010001 0000110010011111000 # cmp b, b\nxx10001001000010010 0000110100011111000 # cmp b, c\nxx10001001000010011 0000110110011111000 # cmp b, d\nxx10001001000010100 0000111000011111000 # cmp b, e\nxx10001001000010101 0000111010011111000 # cmp b, bp\nxx10001001000010110 0000111100011111000 # cmp b, sp\nxx10001001000100000 0001010000011111000 # cmp c, a\nxx10001001000100001 0001010010011111000 # cmp c, b\nxx10001001000100010 0001010100011111000 # cmp c, c\nxx10001001000100011 0001010110011111000 # cmp c, d\nxx10001001000100100 0001011000011111000 # cmp c, e\nxx10001001000100101 0001011010011111000 # cmp c, bp\nxx10001001000100110 0001011100011111000 # cmp c, sp\nxx10001001000110000 0001110000011111000 # cmp d, a\nxx10001001000110001 0001110010011111000 # cmp d, b\nxx10001001000110010 0001110100011111000 # cmp d, c\nxx10001001000110011 0001110110011111000 # cmp d, d\nxx10001001000110100 0001111000011111000 # cmp d, e\nxx10001001000110101 0001111010011111000 # cmp d, bp\nxx10001001000110110 0001111100011111000 # cmp d, sp\nxx10001001001000000 0010010000011111000 # cmp e, a\nxx10001001001000001 0010010010011111000 # cmp e, b\nxx10001001001000010 0010010100011111000 # cmp e, c\nxx10001001001000011 0010010110011111000 # cmp e, d\nxx10001001001000100 0010011000011111000 # cmp e, e\nxx10001001001000101 0010011010011111000 # cmp e, bp\nxx10001001001000110 0010011100011111000 # cmp e, sp\nxx10001001001010000 0010110000011111000 # cmp bp, a\nxx10001001001010001 0010110010011111000 # cmp bp, b\nxx10001001001010010 0010110100011111000 # cmp bp, c\nxx10001001001010011 0010110110011111000 # cmp bp, d\nxx10001001001010100 0010111000011111000 # cmp bp, e\nxx10001001001010101 0010111010011111000 # cmp bp, bp\nxx10001001001010110 0010111100011111000 # cmp bp, sp\nxx10001001001100000 0011010000011111000 # cmp sp, a\nxx10001001001100001 0011010010011111000 # cmp sp, b\nxx10001001001100010 0011010100011111000 # cmp sp, c\nxx10001001001100011 0011010110011111000 # cmp sp, d\nxx10001001001100100 0011011000011111000 # cmp sp, e\nxx10001001001100101 0011011010011111000 # cmp sp, bp\nxx10001001001100110 0011011100011111000 # cmp sp, sp\nxx10001001000001111 0000011110011111000 # cmp a, opd\nxx10001001000011111 0000111110011111000 # cmp b, opd\nxx10001001000101111 0001011110011111000 # cmp c, opd\nxx10001001000111111 0001111110011111000 # cmp d, opd\nxx10001001001001111 0010011110011111000 # cmp e, opd\nxx10001001001011111 0010111110011111000 # cmp bp, opd\nxx10001001001101111 0011011110011111000 # cmp sp, opd\n0x10000110100001111 0000000000000111000 # jnz a (Taken)\n0x10000110100011111 0000100000000111000 # jnz b (Taken)\n0x10000110100101111 0001000000000111000 # jnz c (Taken)\n0x10000110100111111 0001100000000111000 # jnz d (Taken)\n0x10000110101001111 0010000000000111000 # jnz e (Taken)\n0x10000110101011111 0010100000000111000 # jnz bp (Taken)\n0x10000110101101111 0011000000000111000 # jnz sp (Taken)\n1x10000110100001111 0000000000001111000 # jnz a (Skip)\n1x10000110100011111 0000000000001111000 # jnz b (Skip)\n1x10000110100101111 0000000000001111000 # jnz c (Skip)\n1x10000110100111111 0000000000001111000 # jnz d (Skip)\n1x10000110101001111 0000000000001111000 # jnz e (Skip)\n1x10000110101011111 0000000000001111000 # jnz bp (Skip)\n1x10000110101101111 0000000000001111000 # jnz sp (Skip)\n1x10000111000001111 0000000000000111000 # jz a (Taken)\n1x10000111000011111 0000100000000111000 # jz b (Taken)\n1x10000111000101111 0001000000000111000 # jz c (Taken)\n1x10000111000111111 0001100000000111000 # jz d (Taken)\n1x10000111001001111 0010000000000111000 # jz e (Taken)\n1x10000111001011111 0010100000000111000 # jz bp (Taken)\n1x10000111001101111 0011000000000111000 # jz sp (Taken)\n0x10000111000001111 0000000000001111000 # jz a (Skip)\n0x10000111000011111 0000000000001111000 # jz b (Skip)\n0x10000111000101111 0000000000001111000 # jz c (Skip)\n0x10000111000111111 0000000000001111000 # jz d (Skip)\n0x10000111001001111 0000000000001111000 # jz e (Skip)\n0x10000111001011111 0000000000001111000 # jz bp (Skip)\n0x10000111001101111 0000000000001111000 # jz sp (Skip)\nx010000111100001111 0000000000000111000 # jns a (Taken)\nx010000111100011111 0000100000000111000 # jns b (Taken)\nx010000111100101111 0001000000000111000 # jns c (Taken)\nx010000111100111111 0001100000000111000 # jns d (Taken)\nx010000111101001111 0010000000000111000 # jns e (Taken)\nx010000111101011111 0010100000000111000 # jns bp (Taken)\nx010000111101101111 0011000000000111000 # jns sp (Taken)\nx110000111100001111 0000000000001111000 # jns a (Skip)\nx110000111100011111 0000000000001111000 # jns b (Skip)\nx110000111100101111 0000000000001111000 # jns c (Skip)\nx110000111100111111 0000000000001111000 # jns d (Skip)\nx110000111101001111 0000000000001111000 # jns e (Skip)\nx110000111101011111 0000000000001111000 # jns bp (Skip)\nx110000111101101111 0000000000001111000 # jns sp (Skip)\nx110001000000001111 0000000000000111000 # js a (Taken)\nx110001000000011111 0000100000000111000 # js b (Taken)\nx110001000000101111 0001000000000111000 # js c (Taken)\nx110001000000111111 0001100000000111000 # js d (Taken)\nx110001000001001111 0010000000000111000 # js e (Taken)\nx110001000001011111 0010100000000111000 # js bp (Taken)\nx110001000001101111 0011000000000111000 # js sp (Taken)\nx010001000000001111 0000000000001111000 # js a (Skip)\nx010001000000011111 0000000000001111000 # js b (Skip)\nx010001000000101111 0000000000001111000 # js c (Skip)\nx010001000000111111 0000000000001111000 # js d (Skip)\nx010001000001001111 0000000000001111000 # js e (Skip)\nx010001000001011111 0000000000001111000 # js bp (Skip)\nx010001000001101111 0000000000001111000 # js sp (Skip)\nxx10001000100001111 0000000000000111000 # jmp a\nxx10001000100011111 0000100000000111000 # jmp b\nxx10001000100101111 0001000000000111000 # jmp c\nxx10001000100111111 0001100000000111000 # jmp d\nxx10001000101001111 0010000000000111000 # jmp e\nxx10001000101011111 0010100000000111000 # jmp bp\nxx10001000101101111 0011000000000111000 # jmp sp\n1x10001011000001111 0000000000000111000 # je a (Taken)\n1x10001011000011111 0000100000000111000 # je b (Taken)\n1x10001011000101111 0001000000000111000 # je c (Taken)\n1x10001011000111111 0001100000000111000 # je d (Taken)\n1x10001011001001111 0010000000000111000 # je e (Taken)\n1x10001011001011111 0010100000000111000 # je bp (Taken)\n1x10001011001101111 0011000000000111000 # je sp (Taken)\n0x10001011000001111 0000000000001111000 # je a (Skip)\n0x10001011000011111 0000000000001111000 # je b (Skip)\n0x10001011000101111 0000000000001111000 # je c (Skip)\n0x10001011000111111 0000000000001111000 # je d (Skip)\n0x10001011001001111 0000000000001111000 # je e (Skip)\n0x10001011001011111 0000000000001111000 # je bp (Skip)\n0x10001011001101111 0000000000001111000 # je sp (Skip)\n0x10001011100001111 0000000000000111000 # jne a(Taken)\n0x10001011100011111 0000100000000111000 # jne b(Taken)\n0x10001011100101111 0001000000000111000 # jne c(Taken)\n0x10001011100111111 0001100000000111000 # jne d(Taken)\n0x10001011101001111 0010000000000111000 # jne e(Taken)\n0x10001011101011111 0010100000000111000 # jne bp(Taken)\n0x10001011101101111 0011000000000111000 # jne sp(Taken)\n1x10001011100001111 0000000000001111000 # jne a(Skip)\n1x10001011100011111 0000000000001111000 # jne b(Skip)\n1x10001011100101111 0000000000001111000 # jne c(Skip)\n1x10001011100111111 0000000000001111000 # jne d(Skip)\n1x10001011101001111 0000000000001111000 # jne e(Skip)\n1x10001011101011111 0000000000001111000 # jne bp(Skip)\n1x10001011101101111 0000000000001111000 # jne sp(Skip)\n0010001100000001111 0000000000000111000 # ja a (Taken)\n0010001100000011111 0000100000000111000 # ja b (Taken)\n0010001100000101111 0001000000000111000 # ja c (Taken)\n0010001100000111111 0001100000000111000 # ja d (Taken)\n0010001100001001111 0010000000000111000 # ja e (Taken)\n0010001100001011111 0010100000000111000 # ja bp (Taken)\n0010001100001101111 0011000000000111000 # ja sp (Taken)\nxx10001100000001111 0000000000001111000 # ja a (Skip)\nxx10001100000011111 0000000000001111000 # ja b (Skip)\nxx10001100000101111 0000000000001111000 # ja c (Skip)\nxx10001100000111111 0000000000001111000 # ja d (Skip)\nxx10001100001001111 0000000000001111000 # ja e (Skip)\nxx10001100001011111 0000000000001111000 # ja bp (Skip)\nxx10001100001101111 0000000000001111000 # ja sp (Skip)\n0010001100100001111 0000000000000111000 # jae a (Taken)\n0010001100100011111 0000100000000111000 # jae b (Taken)\n0010001100100101111 0001000000000111000 # jae c (Taken)\n0010001100100111111 0001100000000111000 # jae d (Taken)\n0010001100101001111 0010000000000111000 # jae e (Taken)\n0010001100101011111 0010100000000111000 # jae bp (Taken)\n0010001100101101111 0011000000000111000 # jae sp (Taken)\n1010001100100001111 0000000000000111000 # jae a (Taken)\n1010001100100011111 0000100000000111000 # jae b (Taken)\n1010001100100101111 0001000000000111000 # jae c (Taken)\n1010001100100111111 0001100000000111000 # jae d (Taken)\n1010001100101001111 0010000000000111000 # jae e (Taken)\n1010001100101011111 0010100000000111000 # jae bp (Taken)\n1010001100101101111 0011000000000111000 # jae sp (Taken)\nxx10001100100001111 0000000000001111000 # jae a (Skip)\nxx10001100100011111 0000000000001111000 # jae b (Skip)\nxx10001100100101111 0000000000001111000 # jae c (Skip)\nxx10001100100111111 0000000000001111000 # jae d (Skip)\nxx10001100101001111 0000000000001111000 # jae e (Skip)\nxx10001100101011111 0000000000001111000 # jae bp (Skip)\nxx10001100101101111 0000000000001111000 # jae sp (Skip)\n0110001101000001111 0000000000000111000 # jl a (Taken)\n0110001101000011111 0000100000000111000 # jl b (Taken)\n0110001101000101111 0001000000000111000 # jl c (Taken)\n0110001101000111111 0001100000000111000 # jl d (Taken)\n0110001101001001111 0010000000000111000 # jl e (Taken)\n0110001101001011111 0010100000000111000 # jl bp (Taken)\n0110001101001101111 0011000000000111000 # jl sp (Taken)\nxx10001101000001111 0000000000001111000 # jl a (Skip)\nxx10001101000011111 0000000000001111000 # jl b (Skip)\nxx10001101000101111 0000000000001111000 # jl c (Skip)\nxx10001101000111111 0000000000001111000 # jl d (Skip)\nxx10001101001001111 0000000000001111000 # jl e (Skip)\nxx10001101001011111 0000000000001111000 # jl bp (Skip)\nxx10001101001101111 0000000000001111000 # jl sp (Skip)\n0110001101100001111 0000000000000111000 # jle a (Taken)\n0110001101100011111 0000100000000111000 # jle b (Taken)\n0110001101100101111 0001000000000111000 # jle c (Taken)\n0110001101100111111 0001100000000111000 # jle d (Taken)\n0110001101101001111 0010000000000111000 # jle e (Taken)\n0110001101101011111 0010100000000111000 # jle bp (Taken)\n0110001101101101111 0011000000000111000 # jle sp (Taken)\n1010001101100001111 0000000000000111000 # jle a (Taken)\n1010001101100011111 0000100000000111000 # jle b (Taken)\n1010001101100101111 0001000000000111000 # jle c (Taken)\n1010001101100111111 0001100000000111000 # jle d (Taken)\n1010001101101001111 0010000000000111000 # jle e (Taken)\n1010001101101011111 0010100000000111000 # jle bp (Taken)\n1010001101101101111 0011000000000111000 # jle sp (Taken)\nxx10001101100001111 0000000000001111000 # jle a (Skip)\nxx10001101100011111 0000000000001111000 # jle b (Skip)\nxx10001101100101111 0000000000001111000 # jle c (Skip)\nxx10001101100111111 0000000000001111000 # jle d (Skip)\nxx10001101101001111 0000000000001111000 # jle e (Skip)\nxx10001101101011111 0000000000001111000 # jle bp (Skip)\nxx10001101101101111 0000000000001111000 # jle sp (Skip)")) Instruction_Decorder (
    .in({and_5_out, shift_register_1_p5}),
    .out({Instruction_Decorder_out[18], Instruction_Decorder_out_2, Instruction_Decorder_out[13], shift_register_1_p6, Instruction_Decorder_out[9:0]}));
  not not_8 (not_8_out, Instruction_Decorder_out[18]);
  Adder #(.width(16)) adder_1 (
    .a(demultiplexer_2_out0), .b(demultiplexer_3_out0), .out(adder_1_out), .cout(adder_1_cout));  // open: cin
  Subtractor #(.width(16)) subtractor_1 (
    .a(demultiplexer_2_out1), .b(demultiplexer_3_out1), .out(subtractor_1_out), .bout(subtractor_1_bout[0]));  // open: bin
  Multiplier #(.width(16)) multiplier_1 (
    .a(demultiplexer_2_out2), .b(demultiplexer_3_out2), .out(multiplier_1_out));  // open: cin, cout
  assign and_6_out = demultiplexer_2_out3 & demultiplexer_3_out3;  // AND_Gate and_6, 16 bits wide
  assign or_1_out = demultiplexer_2_out4 | demultiplexer_3_out4;  // OR_Gate or_1, 16 bits wide
  assign not_9_out = ~demultiplexer_2_out5;  // NOT_Gate not_9, 16 bits wide
  assign xor_1_out = demultiplexer_2_out6 ^ demultiplexer_3_out6;  // XOR_Gate xor_1, 16 bits wide
  Divider #(.width(16)) divider_1 (
    .a(demultiplexer_3_out7), .b(demultiplexer_2_out7), .out(divider_1_out));  // open: upper, rem
  D_Flip_Flop d_ff_2 (.D(and_5_out[16]), .clk(and_1_out), .Q(d_ff_2_q), .reset(RESET_out));  // open: Qn, preset
  LedBar #(.matrixcols(16)) ledbar_5 (
    .led0(multiplexer_17_out[15]), .led1(multiplexer_17_out[14]), .led2(multiplexer_17_out[13]),
    .led3(multiplexer_17_out[12]), .led4(multiplexer_17_out[11]), .led5(multiplexer_17_out[10]),
    .led6(multiplexer_17_out[9]), .led7(multiplexer_17_out[8]), .led8(multiplexer_17_out[7]),
    .led9(multiplexer_17_out[6]), .led10(multiplexer_17_out[5]), .led11(multiplexer_17_out[4]),
    .led12(multiplexer_17_out[3]), .led13(multiplexer_17_out[2]), .led14(multiplexer_17_out[1]),
    .led15(multiplexer_17_out[0]));
  Multiplexer #(.select(3), .width(16)) multiplexer_17 (
    .in0(adder_1_out), .in1(subtractor_1_out), .in2(multiplier_1_out), .in3(and_6_out), .in4(or_1_out),
    .in5(not_9_out), .in6(xor_1_out), .in7(divider_1_out), .out(multiplexer_17_out),
    .sel(Instruction_Decorder_out[9:7]));
  not not_10 (not_10_out, multiplexer_17_out[0]);
  not not_11 (not_11_out, multiplexer_17_out[1]);
  not not_12 (not_12_out, multiplexer_17_out[2]);
  not not_13 (not_13_out, multiplexer_17_out[3]);
  not not_14 (not_14_out, multiplexer_17_out[4]);
  not not_15 (not_15_out, multiplexer_17_out[5]);
  not not_16 (not_16_out, multiplexer_17_out[6]);
  not not_17 (not_17_out, multiplexer_17_out[7]);
  not not_18 (not_18_out, multiplexer_17_out[8]);
  not not_19 (not_19_out, multiplexer_17_out[9]);
  not not_20 (not_20_out, multiplexer_17_out[10]);
  not not_21 (not_21_out, multiplexer_17_out[11]);
  not not_22 (not_22_out, multiplexer_17_out[12]);
  not not_23 (not_23_out, multiplexer_17_out[13]);
  not not_24 (not_24_out, multiplexer_17_out[14]);
  not not_25 (not_25_out, multiplexer_17_out[15]);
  Register #(.width(16)) FLAGS (
    .D({{14{1'b0}}, subtractor_1_bout}), .en(1'b1), .clk(d_ff_2_q), .Q({FLAGS_q, and_5_out[18:17]}),
    .clr(RESET_out));
  and and_7 (subtractor_1_bout[1], not_17_out, not_10_out, not_11_out, not_12_out, not_13_out, not_14_out, not_15_out, not_16_out, not_18_out, not_19_out, not_20_out, not_21_out, not_22_out, not_23_out, not_24_out, not_25_out);

  // Notes on the sheet:
  //   REGISTERS
endmodule
